# Fritzing sketch SensESP (saved by Fritzing 0.9.4)
circuit board: 9.55cm x 5.55cm
stripboards: 1

parts:
  U4 = SBX DSUN [package=THT]
  WeMos_D1_Mini1 = WeMos D1 Mini
  JP6 = Header 2 [package=molex-1x2_lock]
  JP7 = Header 2 [package=molex-1x2_lock]
  R1 = Resistor [tolerance=±5% resistance=330 package=THT]
  C3 = Electrolytic Capacitor [capacitance=0.47mF voltage=35V package="100 mil [THT, electrolytic]"]
  R2 = Resistor [tolerance=±5% resistance=4.7k package=THT]
  D6 = Schottky Diode [part_number=1N5817 package="300 mil [THT]"]
  D4 = Schottky Diode [part_number=1N5817 package="300 mil [THT]"]
  J1 = Camdenboss CTB0158-2 [part_number=CTB0158-2 package=THT]
  J5 = female pin header, 4 pins [form="♀ (female)"]
  SW1 = DIP Switch 8 Position [package=dipswitch-08]
  D5 = Schottky Diode [part_number=1N5817 package="300 mil [THT]"]
  J6 = female pin header, 4 pins [form="♀ (female)"]
  J7 = female pin header, 4 pins [form="♀ (female)"]
  J8 = female pin header, 4 pins [form="♀ (female)"]

nets:
  N1: U4.GND, WeMos_D1_Mini1.G, JP6.2, JP7.2, C3.-, J1.pin1, J5.pin2, SW1.11
  N2: U4.+VIN, J1.pin2
  N3: U4.+VOUT, D6.anode
  N4: WeMos_D1_Mini1.3V3, D4.anode
  N5: WeMos_D1_Mini1.5V, SW1.1, D5.anode
  N6: WeMos_D1_Mini1.D1, J5.pin3, SW1.10
  N7: WeMos_D1_Mini1.D2, J5.pin4, SW1.9
  N8: WeMos_D1_Mini1.D8, SW1.13
  N9: JP6.1, R1.Pin_0
  N10: JP7.1, C3.+, D6.cathode, SW1.16
  N11: R1.Pin_1, SW1.4
  N12: R2.Pin_0, SW1.5, J6.pin1, J7.pin1, J8.pin1
  N13: R2.Pin_1, SW1.7, J6.pin3, J7.pin3, J8.pin3
  N14: D4.cathode, SW1.15
  N15: J5.pin1, SW1.2, SW1.3, SW1.12
  N16: SW1.6, J6.pin2, J7.pin2, J8.pin2
  N17: SW1.8, J6.pin4, J7.pin4, J8.pin4
  N18: SW1.14, D5.cathode

notes:
  3.3v
  VCC
  GND
  5v
  LED+
  330R
  4K7
  SensESP / Wemos
  24 May 2020
  D1
  D2
  +
  -
  MP1584
  LED
  On/Off

custom parts:
  SBX DSUN: SBX DSUN input voltage 4.5 - 28V DC output voltage .8v to 20VDC (step down converter) Output current 3A max
